# Fritzing sketch PostTrackLog (saved by Fritzing 0.8.7b)
circuit board: 10cm x 6cm
breadboards: 1

parts:
  Part1 = Arduino Pro Mini v13
  IC1 = DS1307 [package=THT]
  Part2 = LilyPad Coin Cell Battery Holder
  R3 = Resistor [tolerance=±5% resistance=1k package=THT]
  R4 = Resistor [tolerance=±5% resistance=1k package=THT]
  Crystal1 = CRYSTAL - kHz [frequency=0pMHz]
  J1 = female pin header, 8 pins [form="♀ (female)"]
  J2 = female pin header, 3 pins [form="♀ (female)"]
  J3 = Screw terminal - 2 pins [package=THT]

nets:
  N1: Part1.A4, IC1.SDA_-_I2C_Data, R4.Pin_0
  N2: Part1.A5, IC1.SCL_-_I2C_Clock, R3.Pin_0
  N3: Part1.GND, IC1.0V, Part2.-, J3.pin1
  N4: Part1.VCC, IC1.+V, R3.Pin_1, R4.Pin_1, J1.pin3, J2.pin3, J3.pin2
  N5: Part1.D13/SCK, J1.pin6
  N6: Part1.D12/MISO, J1.pin7
  N7: Part1.D11_PWM/MOSI, J1.pin5
  N8: Part1.D10_PWM/SS, J1.pin4
  N9: Part1.D2, J2.pin2
  N10: IC1.X1_-_Crystal, Crystal1.pin_0
  N11: IC1.X2_-_Crystal, Crystal1.pin_1
  N12: IC1.Vbat_-_Backup_Supply, Part2.+
  N13: J1.pin1, J2.pin1
